// Digital circuit ALU.dig as structural Verilog
module ALU (
  input  [7:0] A_in,
  input  [7:0] B_in,
  input  O_u,
  input  S_u,
  input  S_m,
  input  S_d,
  input  S_r,
  output [7:0] D_out,
  output carry,
  output [2:0] flags
);

  wire Add_carry, nor_1_out;
  wire [7:0] add_1_s, bitextender_1_out, div_1_q, div_1_r, driver_2_out, xor_1_out;
  wire [15:0] mul_1_mul;
  wire [15:8] driver_4_out;

  assign D_out = O_u ? driver_2_out : 8'bz;  // Driver driver_1
  D_FF d_ff_1 (.D(Add_carry), .C(O_u), .Q(carry));  // open: nQ
  nor nor_1 (nor_1_out, S_r, S_d, S_m);
  assign driver_2_out = S_r ? div_1_r : 8'bz;  // Driver driver_2
  assign driver_2_out = S_d ? div_1_q : 8'bz;  // Driver driver_3
  assign {driver_4_out, driver_2_out} = S_m ? mul_1_mul : 16'bz;  // Driver driver_4
  assign driver_2_out = nor_1_out ? add_1_s : 8'bz;  // Driver driver_5
  Div #(.Bits(8)) div_1 (.a(A_in), .b(xor_1_out), .q(div_1_q), .r(div_1_r));
  Mul #(.Bits(8)) mul_1 (.a(xor_1_out), .b(A_in), .mul(mul_1_mul));
  Add #(.Bits(8)) add_1 (.a(A_in), .b(xor_1_out), .c_i(S_u), .s(add_1_s), .c_o(Add_carry));
  assign xor_1_out = B_in ^ bitextender_1_out;  // XOr xor_1, 8 bits wide
  BitExtender #(.inputBits(1), .outputBits(8)) bitextender_1 (.in(S_u), .out(bitextender_1_out));
  Comparator #(.Bits(8)) comparator_1 (.a(A_in), .b(B_in), .gt(flags[0]), .eq(flags[1]), .lt(flags[2]));

  // Other names for the same wires on the sheet: Sd = S_d; Sm = S_m; Sr = S_r; Su = S_u
endmodule
