// Digital circuit A_register.dig as structural Verilog
module A_register (
  input  [7:0] D_in,
  input  L_a,
  input  O_a,
  input  clk,
  output [7:0] D_out,
  output [7:0] ALU_a,
  output [7:0] A_const
);

  assign D_out = O_a ? A_const : 8'bz;  // Driver driver_1
  Register #(.Bits(8)) register_1 (.D(D_in), .C(clk), .en(L_a), .Q(A_const));

  assign ALU_a = A_const;
endmodule
