// Digital circuit B_register.dig as structural Verilog
module B_register (
  input  [7:0] D_in,
  input  L_b,
  input  clk,
  input  O_b,
  input  carry,
  input  B_car,
  output [7:0] ALU_b,
  output [7:0] B_const,
  output [7:0] D_out
);

  wire [7:0] add_1_s, multiplexer_1_out;

  assign D_out = O_b ? ALU_b : 8'bz;  // Driver driver_1
  Register #(.Bits(8)) register_1 (.D(multiplexer_1_out), .C(clk), .en(L_b), .Q(ALU_b));
  Multiplexer #(.Bits(8)) multiplexer_1 (.sel(B_car), .in_0(D_in), .in_1(add_1_s), .out(multiplexer_1_out));
  Add #(.Bits(8)) add_1 (.a(ALU_b), .b({8{1'b0}}), .c_i(carry), .s(add_1_s));  // open: c_o

  assign B_const = ALU_b;
endmodule
