// Digital circuit Controller.dig as structural Verilog
module Controller (
  input  [7:0] instruction,
  input  E,
  input  On,
  input  clk,
  output O_pc,
  output L_mar,
  output O_mem,
  output L_ir,
  output I_pc,
  output clk_o,
  output L_a,
  output O_a,
  output S_u,
  output O_u,
  output L_b,
  output L_o,
  output lt,
  output eq,
  output gt,
  output C_mem,
  output L_ram,
  output O_b,
  output C_i,
  output U_h,
  output U_t,
  output O_kb,
  output [2:0] LED,
  output S_m,
  output S_d,
  output S_r,
  output L_sp1,
  output O_sp,
  output L_sp2,
  output B_car
);

  wire and_4_out, clk_stop, comparator_1_eq, \end , xor_1_out;
  wire [3:0] counter_1_out;
  wire [14:14] rom_1_d;

  and and_1 (LED[2], On, ~comparator_1_eq, clk_stop);  // And
  and and_2 (LED[1], On, ~comparator_1_eq, ~clk_stop);  // And
  and and_3 (LED[0], On, comparator_1_eq, ~clk_stop);  // And
  and and_4 (and_4_out, clk, On);
  xor xor_1 (xor_1_out, ~E, clk_stop);  // XOr
  Comparator #(.Bits(8)) comparator_1 (.a(instruction), .b({8{1'b1}}), .eq(comparator_1_eq));  // open: gt, lt
  and and_5 (clk_o, ~comparator_1_eq, xor_1_out, and_4_out);  // And
  Counter #(.Bits(4)) counter_1 (.en(clk_o), .C(clk_o), .clr(\end ), .out(counter_1_out));  // open: ovf
  // Probe on counter_1_out
  // Probe on {instruction, counter_1_out}
  ROM #(.AddrBits(12), .Bits(31)) rom_1 (
    .A({instruction, counter_1_out}), .sel(1'b1),
    .D({B_car, \end , clk_stop, O_sp, L_sp2, L_sp1, O_kb, U_t, U_h, C_i, gt, eq, lt, L_o, L_ir, L_ram, rom_1_d[14], O_mem, C_mem, O_u, S_r, S_d, S_m, S_u, L_mar, O_b, L_b, O_a, L_a, I_pc, O_pc}));
  // Probe on {B_car, \end , clk_stop, O_sp, L_sp2, L_sp1, O_kb, U_t, U_h, C_i, gt, eq, lt, L_o, L_ir, L_ram, rom_1_d[14], O_mem, C_mem, O_u, S_r, S_d, S_m, S_u, L_mar, O_b, L_b, O_a, L_a, I_pc, O_pc}

  // Notes on the sheet:
  //   contents of rom_1 (hex, n*v repeats v):
  //   41,12002,254*0,41,12002,41,20002006,12*0,41,12002,41,2002002,41
  //   ,4002002,8000040,20003004,8*0,41,12002,41,2002002,41,4002002,8000040
  //   ,20008008,8*0,41,12002,8000040,20003004,12*0,41,12002,8000040
  //   ,20008008,188*0,41,12002,41,20002012,12*0,41,12002,41,2002002
  //   ,41,4002002,8000040,20003010,8*0,41,12002,41,2002002,41,4002002
  //   ,8000040,20008020,8*0,41,12002,60000010,205*0,41,12002,20000804
  //   ,13*0,41,12002,20000884,13*0,41,12002,20000904,13*0,41,12002,20000a04
  //   ,13*0,41,12002,20000c04,189*0,41,12002,41,2002002,41,4002002,281c0000
  //   ,9*0,41,12002,41,2002002,41,4002002,28040000,9*0,41,12002,41,2002002
  //   ,41,4002002,28080000,9*0,41,12002,41,2002002,41,4002002,28100000
  //   ,9*0,41,12002,41,2002002,41,4002002,280c0000,9*0,41,12002,41,2002002
  //   ,41,4002002,28180000,9*0,41,12002,41,2002002,41,4002002,28140000
  //   ,153*0,41,12002,2000008,24000020,2300*0,41,12002,620008,a20008
  //   ,20220008,11*0,41,12002,20020008,141*0,41,12002,31000004,13*0
  //   ,41,12002,31000010
endmodule
