// Digital circuit Flags.dig as structural Verilog
module Flags (
  input  gt_f,
  input  eq_f,
  input  lt_f,
  input  [2:0] flags,
  output j
);

  wire and_1_out, and_2_out, and_3_out;

  and and_1 (and_1_out, flags[0], gt_f);
  and and_2 (and_2_out, eq_f, flags[1]);
  and and_3 (and_3_out, flags[2], lt_f);
  or or_1 (j, and_1_out, and_2_out, and_3_out);
endmodule
