// Digital circuit IR.dig as structural Verilog
module IR (
  input  L_ir,
  input  [7:0] D_in,
  input  clk,
  output [7:0] to_controller
);

  Register #(.Bits(8)) register_1 (.D(D_in), .C(clk), .en(L_ir), .Q(to_controller));
  // Pins of 4 and 8 bits meet at to_controller
endmodule
