// Digital circuit KB.dig as structural Verilog
module KB (
  input  O_kb,
  input  enter_dig,
  output [7:0] D_out,
  output [7:0] KB_const
);

  wire comparator_1_gt, kb_av, kb_clk;
  wire [7:0] add_1_s, mul_1_mul;
  wire [15:0] kb_data, multiplexer_1_out, sub_1_s, sub_2_s;
  wire [15:8] mul_1_mul_2;

  Comparator #(.Bits(16)) comparator_1 (.a(16'h40), .b(kb_data), .gt(comparator_1_gt));  // open: eq, lt
  Sub #(.Bits(16)) sub_1 (.a(kb_data), .b(16'h37), .c_i(1'b0), .s(sub_1_s));  // open: c_o
  Sub #(.Bits(16)) sub_2 (.a(kb_data), .b(16'h30), .c_i(1'b0), .s(sub_2_s));  // open: c_o
  Multiplexer #(.Bits(16)) multiplexer_1 (
    .sel(comparator_1_gt), .in_0(sub_1_s), .in_1(sub_2_s), .out(multiplexer_1_out));
  Keyboard keyboard_1 (.C(kb_clk), .en(1'b1), .D(kb_data), .av(kb_av));
  and and_1 (kb_clk, kb_av, enter_dig);
  Add #(.Bits(8)) add_1 (.a(mul_1_mul), .b(multiplexer_1_out[7:0]), .c_i(1'b0), .s(add_1_s));  // open: c_o
  Mul #(.Bits(8)) mul_1 (.a(8'h10), .b(KB_const), .mul({mul_1_mul_2, mul_1_mul}));
  Register #(.Bits(8)) register_1 (.D(add_1_s), .C(kb_clk), .en(1'b1), .Q(KB_const));
  assign D_out = O_kb ? KB_const : 8'bz;  // Driver driver_1
endmodule
