// Digital circuit MAR.dig as structural Verilog
module MAR (
  input  [15:0] addr_in,
  input  L_mar,
  input  clk,
  output [15:0] to_mem
);

  Register #(.Bits(16)) register_1 (.D(addr_in), .C(clk), .en(L_mar), .Q(to_mem));
endmodule
