// Digital circuit Main.dig as structural Verilog
module Main (
  input  clk
);

  wire alu_1_carry, B_car, button_1_out, button_2_out, C_i, C_mem, clk_t, controller_1_p19, dipswitch_1_out,
       eq, gt, I_pc, j, L_a, L_b, L_ir, L_mar, L_o, L_ram, L_sp1, L_sp2, lt, O_a, O_b, O_kb, O_mem, O_pc,
       O_sp, O_u, S_d, S_m, S_r, S_u, U_h, U_t;
  wire [2:0] alu_1_flags, rgbled_1_p3;
  wire [3:0] kb_1_kb_const, kb_1_kb_const_2;
  wire [7:0] a_register_1_a_const, a_register_1_alu_a, b_register_1_alu_b, b_register_1_b_const,
       outputdecoder_1_o_const, outputdecoder_1_o_o, ramrom_1_d_out, ramrom_1_mem_const;
  wire [15:0] mar_1_to_mem, pc_1_addr_out, pc_1_pc_const, stackpointer_1_sp1_const, stackpointer_1_sp2_const,
       stackpointer_1_sp_const;

  // RGBLED rgbled_1: pin names not known; wires that end beside it: rgbled_1_p3[2], rgbled_1_p3[1], rgbled_1_p3[0]
  Button button_1 (.out(button_1_out));
  DipSwitch dipswitch_1 (.out(dipswitch_1_out));
  // Controller controller_1: pin names not known; wires that end beside it: rgbled_1_p3, button_1_out, clk, dipswitch_1_out, clk_t, O_pc, I_pc, L_a, O_a, L_b, O_b, L_mar, S_u, S_m, S_d, S_r, O_u, C_mem, controller_1_p19, O_mem, L_ram, L_ir, L_o, lt, eq
  // Probe on pc_1_addr_out
  PC pc_1 (
    .j(j), .I_pc(I_pc), .clk(clk_t), .O_pc(O_pc), .addr_in(pc_1_addr_out), .addr_out(pc_1_addr_out),
    .pc_const(pc_1_pc_const));
  MAR mar_1 (.addr_in(pc_1_addr_out), .clk(clk_t), .L_mar(L_mar), .to_mem(mar_1_to_mem));
  RAMROM ramrom_1 (
    .mem_const(ramrom_1_mem_const), .D_out(ramrom_1_d_out), .D_in(ramrom_1_d_out), .from_mar(mar_1_to_mem),
    .C_mem(C_mem), .O_mem(O_mem), .L_ram(L_ram), .clk(clk_t));
  StackPointer stackpointer_1 (
    .SP_out(pc_1_addr_out), .O_sp(O_sp), .clk(clk_t), .L_sp2(L_sp2), .L_sp1(L_sp1), .D_in(ramrom_1_d_out),
    .SP_const(stackpointer_1_sp_const), .SP2_const(stackpointer_1_sp2_const),
    .SP1_const(stackpointer_1_sp1_const));
  // IR ir_1: pin names not known; wires that end beside it: clk_t, L_ir, controller_1_p19, ramrom_1_d_out
  Seven_Seg_Hex seven_seg_hex_1 (.d(kb_1_kb_const_2), .dp(1'b0));
  Button button_2 (.out(button_2_out));
  // Probe on mar_1_to_mem
  // Probe on controller_1_p19
  Seven_Seg_Hex seven_seg_hex_2 (.d(kb_1_kb_const), .dp(1'b0));
  KB kb_1 (.D_out(ramrom_1_d_out), .KB_const({kb_1_kb_const_2, kb_1_kb_const}), .O_kb(O_kb), .enter_dig(button_2_out));
  // Probe on ramrom_1_mem_const
  // Probe on pc_1_pc_const
  // Probe on stackpointer_1_sp_const
  // Probe on stackpointer_1_sp2_const
  // Probe on stackpointer_1_sp1_const
  // Probe on ramrom_1_d_out
  A_register a_register_1 (
    .D_in(ramrom_1_d_out), .D_out(ramrom_1_d_out), .L_a(L_a), .clk(clk_t), .O_a(O_a),
    .ALU_a(a_register_1_alu_a), .A_const(a_register_1_a_const));
  ALU alu_1 (
    .A_in(a_register_1_alu_a), .B_in(b_register_1_alu_b), .carry(alu_1_carry), .D_out(ramrom_1_d_out),
    .flags(alu_1_flags), .S_u(S_u), .S_m(S_m), .O_u(O_u), .S_d(S_d), .S_r(S_r));
  B_register b_register_1 (
    .D_out(ramrom_1_d_out), .D_in(ramrom_1_d_out), .B_const(b_register_1_b_const), .L_b(L_b), .clk(clk_t),
    .O_b(O_b), .B_car(B_car), .ALU_b(b_register_1_alu_b), .carry(alu_1_carry));
  OutputDecoder outputdecoder_1 (
    .D_in(ramrom_1_d_out), .C_i(C_i), .O_const(outputdecoder_1_o_const), .O_o(outputdecoder_1_o_o),
    .U_h(U_h), .U_t(U_t));
  // Probe on a_register_1_a_const
  // Probe on b_register_1_b_const
  // Probe on outputdecoder_1_o_const
  Flags flags_1 (.gt_f(gt), .eq_f(eq), .lt_f(lt), .j(j), .flags(alu_1_flags));
  Terminal terminal_1 (.D(outputdecoder_1_o_o), .C(clk_t), .en(L_o));

  // Notes on the sheet:
  //   clk: Hz: 2147483647
endmodule
