// Digital circuit OutputDecoder.dig as structural Verilog
module OutputDecoder (
  input  [7:0] D_in,
  input  C_i,
  input  U_h,
  input  U_t,
  output [7:0] O_o,
  output [7:0] O_const
);

  wire [7:0] add_1_s, multiplexer_1_out, multiplexer_2_out, rom_1_d, rom_2_d, rom_3_d;

  ROM #(.AddrBits(8), .Bits(8)) rom_1 (.A(D_in), .sel(1'b1), .D(rom_1_d));
  ROM #(.AddrBits(8), .Bits(8)) rom_2 (.A(D_in), .sel(1'b1), .D(rom_2_d));
  ROM #(.AddrBits(8), .Bits(8)) rom_3 (.A(D_in), .sel(1'b1), .D(rom_3_d));
  Multiplexer #(.Bits(8)) multiplexer_1 (.sel(U_t), .in_0(rom_1_d), .in_1(rom_2_d), .out(multiplexer_1_out));
  Add #(.Bits(8)) add_1 (.a(multiplexer_2_out), .b(8'h30), .c_i(1'b0), .s(add_1_s));  // open: c_o
  Multiplexer #(.Bits(8)) multiplexer_2 (.sel(U_h), .in_0(multiplexer_1_out), .in_1(rom_3_d), .out(multiplexer_2_out));
  Multiplexer #(.Bits(8)) multiplexer_3 (.sel(C_i), .in_0(D_in), .in_1(add_1_s), .out(O_o));

  assign O_const = D_in;

  // Notes on the sheet:
  //   contents of rom_1 (hex, n*v repeats v):
  //   0,1,2,3,4,5,6,7,8,9,0,1,2,3,4,5,6,7,8,9,0,1,2,3,4,5,6,7,8,9,0
  //   ,1,2,3,4,5,6,7,8,9,0,1,2,3,4,5,6,7,8,9,0,1,2,3,4,5,6,7,8,9,0,1
  //   ,2,3,4,5,6,7,8,9,0,1,2,3,4,5,6,7,8,9,0,1,2,3,4,5,6,7,8,9,0,1,2
  //   ,3,4,5,6,7,8,9,0,1,2,3,4,5,6,7,8,9,0,1,2,3,4,5,6,7,8,9,0,1,2,3
  //   ,4,5,6,7,8,9,0,1,2,3,4,5,6,7,8,9,0,1,2,3,4,5,6,7,8,9,0,1,2,3,4
  //   ,5,6,7,8,9,0,1,2,3,4,5,6,7,8,9,0,1,2,3,4,5,6,7,8,9,0,1,2,3,4,5
  //   ,6,7,8,9,0,1,2,3,4,5,6,7,8,9,0,1,2,3,4,5,6,7,8,9,0,1,2,3,4,5,6
  //   ,7,8,9,0,1,2,3,4,5,6,7,8,9,0,1,2,3,4,5,6,7,8,9,0,1,2,3,4,5,6,7
  //   ,8,9,0,1,2,3,4,5
  //   contents of rom_2 (hex, n*v repeats v):
  //   10*0,10*1,10*2,10*3,10*4,10*5,10*6,10*7,10*8,10*9,10*0,10*1,10*2
  //   ,10*3,10*4,10*5,10*6,10*7,10*8,10*9,10*0,10*1,10*2,10*3,10*4,6*5
  //   contents of rom_3 (hex, n*v repeats v):
  //   100*0,100*1,56*2
endmodule
