// Digital circuit PC.dig as structural Verilog
module PC (
  input  j,
  input  I_pc,
  input  clk,
  input  O_pc,
  input  [15:0] addr_in,
  output [15:0] addr_out,
  output [15:0] pc_const
);

  wire or_1_out;
  wire [15:0] multiplexer_1_out, PC_inc;

  or or_1 (or_1_out, I_pc, j);
  Multiplexer #(.Bits(16)) multiplexer_1 (.sel(I_pc), .in_0(addr_in), .in_1(PC_inc), .out(multiplexer_1_out));
  assign addr_out = O_pc ? pc_const : 16'bz;  // Driver driver_1
  Register #(.Bits(16)) register_1 (.D(multiplexer_1_out), .C(clk), .en(or_1_out), .Q(pc_const));
  Add #(.Bits(16)) add_1 (.a(16'h1), .b(pc_const), .c_i(1'b0), .s(PC_inc));  // open: c_o
endmodule
