// Digital circuit RAMROM.dig as structural Verilog
module RAMROM (
  input  [15:0] from_mar,
  input  O_mem,
  input  [7:0] D_in,
  input  L_ram,
  input  clk,
  input  C_mem,
  output [7:0] D_out,
  output [7:0] mem_const
);

  wire [7:0] ramdualport_1_d, rom_1_d;

  ROM #(.AddrBits(16), .Bits(8)) rom_1 (.A(from_mar), .sel(1'b1), .D(rom_1_d));
  RAMDualPort #(.AddrBits(16), .Bits(8)) ramdualport_1 (
    .A(from_mar), .Din(D_in), .str(L_ram), .C(clk), .ld(C_mem), .D(ramdualport_1_d));
  Multiplexer #(.Bits(8)) multiplexer_1 (.sel(C_mem), .in_0(rom_1_d), .in_1(ramdualport_1_d), .out(mem_const));
  assign D_out = O_mem ? mem_const : 8'bz;  // Driver driver_1

  // Notes on the sheet:
  //   contents of rom_1 (hex, n*v repeats v):
  //   10,2,12,ff,ff,11,ff,ff,12,0,0,10,ff,12,1,0,11,0,0,21,1,0,41,1c
  //   ,0,40,a6,0,10,1,12,fe,ff,10,2,12,fd,ff,11,fd,ff,12,0,0,11,ff,ff
  //   ,12,1,0,11,0,0,21,1,0,41,3e,0,40,76,0,11,fd,ff,12,0,0,11,ff,ff
  //   ,21,0,0,34,12,0,0,10,0,12,1,0,11,0,0,21,1,0,42,5f,0,40,64,0,10
  //   ,0,12,fe,ff,10,1,12,0,0,11,fd,ff,21,0,0,30,12,fd,ff,40,26,0,11
  //   ,fe,ff,12,0,0,10,1,12,1,0,11,0,0,21,1,0,42,8d,0,40,94,0,11,ff,ff
  //   ,e0,10,a,e1,10,1,12,0,0,11,ff,ff,21,0,0,30,12,ff,ff,40,5,0,ff
endmodule
