// Digital circuit StackPointer.dig as structural Verilog
module StackPointer (
  input  [7:0] D_in,
  input  clk,
  input  L_sp1,
  input  L_sp2,
  input  O_sp,
  output [15:0] SP_out,
  output [15:0] SP_const,
  output [15:0] SP2_const,
  output [15:0] SP1_const
);

  Register #(.Bits(8)) register_1 (.D(D_in), .C(clk), .en(L_sp2), .Q(SP2_const[7:0]));
  Register #(.Bits(8)) register_2 (.D(D_in), .C(clk), .en(L_sp1), .Q(SP1_const[7:0]));
  assign SP_out = O_sp ? {SP2_const[7:0], SP1_const[7:0]} : 16'bz;  // Driver driver_1
  // Pins of 8 and 16 bits meet at SP1_const
  // Pins of 8 and 16 bits meet at SP2_const

  assign SP_const = {SP2_const[7:0], SP1_const[7:0]};
endmodule
